// Digital circuit Processador acho.dig as structural Verilog
module Processador_acho (
);

  wire ctrl_ula_1_p3, ctrl_ula_1_p4, ctrl_ula_1_p5, MUX_PC, uc_1_p4;
  wire [1:0] register_1_q;
  wire [15:0] IR_q, \Memória_d , multiplexer_1_out, multiplexer_2_out, multiplexer_3_out, multiplexer_4_out,
       PC_q, reginaldos_1_p4, reginaldos_1_p5, uc_1_p2, ula_1_s, ULA_out_q, ULAA_q, ULAB_q;
  wire [15:3] reginaldos_1_p1, reginaldos_1_p2, undriven;

  Register #(.Bits(16)) PC (.Q(PC_q));  // open: D, C, en
  Multiplexer #(.Bits(16)) multiplexer_1 (.sel(MUX_PC), .in_0(PC_q), .out(multiplexer_1_out));  // open: in_1
  RAMDualPort #(.AddrBits(16), .Bits(16)) \Memória  (.A(multiplexer_1_out), .D(\Memória_d ));  // open: Din, str, C, ld
  Register #(.Bits(16)) IR (.C(\Memória_d [0]), .Q(IR_q));  // open: D, en
  Register register_1 (.Q(register_1_q[0]));  // open: D, C, en
  Multiplexer #(.Selector_Bits(2), .Bits(16)) multiplexer_2 (
    .sel(register_1_q), .in_0({reginaldos_1_p1, IR_q[11:9]}), .in_1({reginaldos_1_p2, IR_q[8:6]}),
    .in_2({undriven, IR_q[5:3]}), .out(multiplexer_2_out));  // open: in_3
  // Reginaldos reginaldos_1: pin names not known; wires that end beside it: {reginaldos_1_p1, IR_q[11:9]}, {reginaldos_1_p2, IR_q[8:6]}, multiplexer_2_out, reginaldos_1_p4, reginaldos_1_p5
  // UC uc_1: pin names not known; wires that end beside it: IR_q[15:12], uc_1_p2, MUX_PC, uc_1_p4
  BitExtender Ext_Sinal (.in(IR_q[15:8]), .out(uc_1_p2));
  Register #(.Bits(16)) ULAB (.D(reginaldos_1_p5), .Q(ULAB_q));  // open: C, en
  Register #(.Bits(16)) ULAA (.D(reginaldos_1_p4), .Q(ULAA_q));  // open: C, en
  // Ctrl_ULA ctrl_ula_1: pin names not known; wires that end beside it: uc_1_p2, IR_q[2:0], ctrl_ula_1_p3, ctrl_ula_1_p4, ctrl_ula_1_p5
  Multiplexer #(.Selector_Bits(2), .Bits(16)) multiplexer_3 (
    .in_1(ULAB_q), .in_2(16'h1), .in_3(uc_1_p2), .out(multiplexer_3_out));  // open: sel, in_0
  Multiplexer #(.Bits(16)) multiplexer_4 (.sel(uc_1_p4), .in_0(PC_q), .in_1(ULAA_q), .out(multiplexer_4_out));
  ULA ula_1 (
    .A(multiplexer_4_out), .B(multiplexer_3_out), .Ainv(ctrl_ula_1_p3), .Binv(ctrl_ula_1_p4),
    .Cin(ctrl_ula_1_p5), .S(ula_1_s));  // open: OP, Cout, Zero, Overflow
  Register #(.Bits(16)) ULA_out (.D(ula_1_s), .Q(ULA_out_q));  // open: C, en
  // Pins of 1 and 16 bits meet at \Memória_d 
  // Pins of 3 and 16 bits meet at {undriven, IR_q[5:3]}
  // Pins of 3 and 16 bits meet at {reginaldos_1_p2, IR_q[8:6]}
  // Pins of 3 and 16 bits meet at {reginaldos_1_p1, IR_q[11:9]}
  // Pins of 1 and 2 bits meet at register_1_q
endmodule
